# Fritzing sketch PresenDuino (saved by Fritzing 0.8.7b)
breadboards: 1

parts:
  Part1 = Arduino Uno (Rev3)
  LCD1 = LCD screen
  S1 = Pushbutton [package="[THT]"]
  S2 = Pushbutton [package="[THT]"]
  R1 = Resistor [tolerance=±5% resistance=1k package=THT]
  R1_2 = Resistor [tolerance=±5% resistance=1k package=THT]
  R2 = Rotary Potentiometer (Small) [maximum_resistance=100kΩ package=THT]
  xbee1 = Adafruit Xbee Adapter v1.1 [part_number=126]

nets:
  N1: Part1.D8, xbee1.tx
  N2: Part1.D9_PWM, xbee1.rx
  N3: Part1.D11_PWM/MOSI, LCD1.E
  N4: Part1.D12/MISO, LCD1.RS
  GND: Part1.GND, LCD1.VSS, LCD1.R/W, S1.Pin_3, S1.Pin_4, S2.Pin_3, S2.Pin_4, R2.leg1, xbee1.gnd
  N5: Part1.D2, S2.Pin_1, S2.Pin_2, R1.Pin_1
  N6: Part1.D3_PWM, S1.Pin_1, S1.Pin_2, R1_2.Pin_1
  N7: Part1.D4, LCD1.DB7
  N8: Part1.D5_PWM, LCD1.DB6
  N9: Part1.D6_PWM, LCD1.DB5
  N10: Part1.D7, LCD1.DB4
  5V: Part1.5V, LCD1.VDD, R1.Pin_0, R1_2.Pin_0, R2.leg2, xbee1.3v#10
  N11: LCD1.V0, R2.wiper

custom parts:
  Adafruit Xbee Adapter v1.1: Adafruit Xbee Adapter
