# Fritzing sketch SignalSide (saved by Fritzing 0.8.7b)
breadboards: 1

parts:
  Part1 = Arduino Uno (Rev3)
  xbee1 = Adafruit Xbee Adapter v1.1 [part_number=126]
  LED1 = LED - 5mm [color="Red (633nm)" package="5 mm [THT]"]
  LED2 = LED - 5mm [color="Red (633nm)" package="5 mm [THT]"]
  LED3 = LED - 5mm [color="Red (633nm)" package="5 mm [THT]"]
  R1 = Resistor [tolerance=±20% resistance=220 package=THT]
  R2 = Resistor [tolerance=±20% resistance=220 package=THT]
  R3 = Resistor [tolerance=±20% resistance=220 package=THT]

nets:
  N1: Part1.D8, xbee1.tx
  N2: Part1.D9_PWM, xbee1.rx
  N3: Part1.D11_PWM/MOSI, R3.Pin_0
  N4: Part1.D12/MISO, R2.Pin_0
  N5: Part1.D13/SCK, R1.Pin_0
  N6: Part1.5V, xbee1.3v#10
  GND: Part1.GND, xbee1.gnd
  N7: LED1.cathode, LED2.cathode, LED3.cathode
  N8: LED1.anode, R1.Pin_1
  N9: LED2.anode, R3.Pin_1
  N10: LED3.anode, R2.Pin_1

custom parts:
  Adafruit Xbee Adapter v1.1: Adafruit Xbee Adapter
